// Logisim project m1_33448.circ as structural Verilog
module NOR_T (
  input  x,
  input  y,
  output z
);

  wire transistor_1_out;

  Transistor transistor_1 (.in(1'b1), .out(transistor_1_out), .gate(x));
  Transistor #(.\type ("n")) transistor_2 (.in(1'b0), .out(z), .gate(x));
  Transistor #(.\type ("n")) transistor_3 (.in(1'b0), .out(z), .gate(y));
  Transistor transistor_4 (.in(transistor_1_out), .out(z), .gate(y));
endmodule

module NOT_NOR (
  input  x,
  output y
);

  NOR_T nor_t_1 (.x(x), .y(x), .z(y));
endmodule

module OR_NOR (
  input  x,
  input  y,
  output z
);

  wire nor_t_1_z;

  NOR_T nor_t_1 (.x(x), .y(y), .z(nor_t_1_z));
  NOR_T nor_t_2 (.x(nor_t_1_z), .y(nor_t_1_z), .z(z));
endmodule

module AND_NOR (
  input  x,
  input  y,
  output z
);

  wire nor_t_1_z, nor_t_3_z;

  NOR_T nor_t_1 (.x(x), .y(x), .z(nor_t_1_z));
  NOR_T nor_t_2 (.x(nor_t_1_z), .y(nor_t_3_z), .z(z));
  NOR_T nor_t_3 (.x(y), .y(y), .z(nor_t_3_z));
endmodule

module XOR_SOP (
  input  in_1,
  input  in_2,
  output out_3
);

  wire and_nor_1_z, and_nor_2_z, not_nor_1_y, not_nor_2_y;

  NOT_NOR not_nor_1 (.x(in_1), .y(not_nor_1_y));
  AND_NOR and_nor_1 (.x(not_nor_1_y), .y(in_2), .z(and_nor_1_z));
  OR_NOR or_nor_1 (.x(and_nor_1_z), .y(and_nor_2_z), .z(out_3));
  NOT_NOR not_nor_2 (.x(in_2), .y(not_nor_2_y));
  AND_NOR and_nor_2 (.x(in_1), .y(not_nor_2_y), .z(and_nor_2_z));
endmodule
